# Fritzing sketch l293d (saved by Fritzing 0.9.3b)
breadboards: 1

parts:
  M1 = DC Motor
  Bauteil1 = Arduino Uno (Rev3)
  IC1 = L293D [package=THT]
  Power_plug1 = Power plug

nets:
  N1: M1.pin_1, IC1.Out_4_(_Controlled_by_Enable_2_)
  N2: M1.pin_2, IC1.Out_3_(_Controlled_by_Enable_2_)
  N3: Bauteil1.D9_PWM, IC1.Enable_2
  N4: Bauteil1.D10_PWM/SS, IC1.In_4
  N5: Bauteil1.D11_PWM/MOSI, IC1.In_3
  GND: Bauteil1.GND, IC1.0V, Power_plug1.GND
  N6: Bauteil1.5V, IC1.+V
  VIN: Bauteil1.VIN, IC1.+Vmotor, Power_plug1.VCC

notes:
  9V DC is enough
