# Fritzing sketch dc-motor-no-arduino (saved by Fritzing 0.9.2b)
breadboards: 1

parts:
  R1 = Rotary Potentiometer (Large) [maximum_resistance=100kΩ package=THT]
  M1 = DC Motor
  VCC1 = Battery block 9V

nets:
  N1: R1.leg1, VCC1.+
  N2: R1.wiper, M1.pin_1
  N3: R1.leg2, M1.pin_2, VCC1.-
