# Fritzing sketch infraredio (saved by Fritzing 0.8.3b)
breadboards: 1

parts:
  Bauteil1 = Arduino Uno (Rev3)
  IR1 = TSOP312.., 314.. [package=THT]
  LED1 = LED - 5mm [color="Red (633nm)" package="5 mm [THT]"]
  R1 = Resistor [tolerance=±5% resistance=220 package=THT]

nets:
  N1: Bauteil1.A0, IR1.GND
  N2: Bauteil1.ICSP_SCK, Bauteil1.D13/SCK, R1.Pin_1
  N3: Bauteil1.GND, LED1.cathode
  N4: Bauteil1.5V, IR1.Vs, IR1.Data
  N5: LED1.anode, R1.Pin_0
