# Fritzing sketch lightTheremin (saved by Fritzing 0.8.3b)
breadboards: 1

parts:
  Bauteil1 = Arduino Uno (Rev3)
  R1 = Photocell (LDR) [package=THT]
  J1 = Piezo Speaker
  R2 = Resistor [tolerance=±5% resistance=10k package=THT]

nets:
  N1: Bauteil1.A0, R1.pin_1, R2.Pin_0
  N2: Bauteil1.GND, J1.pin1
  N3: Bauteil1.D9_PWM, J1.pin2
  N4: Bauteil1.5V, R1.pin_0, R2.Pin_1

notes:
  see this video http://www.youtube.com/watch?v=57S3dylfw3I
