# Fritzing sketch piezo_output (saved by Fritzing 0.9.1b)
breadboards: 1

parts:
  Part1 = Arduino Uno (Rev3)
  R1 = Resistor [tolerance=±5% resistance=220 package=THT]
  J1 = Piezo Speaker

nets:
  N1: Part1.D12/MISO, R1.Pin_0
  N2: Part1.GND, J1.pin1
  N3: R1.Pin_1, J1.pin2
