# Fritzing sketch piezo-generate-current (saved by Fritzing 0.9.3b)
breadboards: 1

parts:
  D1 = Rectifier Diode [part_number=1N4001 package="300 mil [THT]"]
  D2 = Rectifier Diode [part_number=1N4001 package="300 mil [THT]"]
  D3 = Rectifier Diode [part_number=1N4001 package="300 mil [THT]"]
  LED1 = LED - 5mm [color="Red (633nm)" package="5 mm [THT]"]
  J1 = Piezo Speaker
  D4 = Rectifier Diode [part_number=1N4001 package="300 mil [THT]"]

nets:
  N1: D1.cathode, D3.anode, J1.pin2
  N2: D1.anode, D2.anode, LED1.cathode
  N3: D2.cathode, J1.pin1, D4.anode
  N4: D3.cathode, LED1.anode, D4.cathode
