# Fritzing sketch potentiometer (saved by Fritzing 0.9.0b)
breadboards: 1

parts:
  R1 = Rotary Potentiometer (Small) [maximum_resistance=10kΩ package=THT]
  Bauteil1 = Arduino Uno (Rev3)

nets:
  N1: R1.leg1, Bauteil1.GND
  N2: R1.wiper, Bauteil1.A0
  N3: R1.leg2, Bauteil1.5V

notes:
  /**
  * A very simple sketch by Fabian Morón Zirfas
  *
  *
  */
  int poti = A0; // the poti pin
  void setup(){
  Serial.begin(9600); // init Serial
  }
  void loop(){
  int potival = analogRead(poti); // read the poti
  Serial.println(potival); // print it
  delay(100);// wait a bit
  }
