# Fritzing sketch potentiometer (saved by Fritzing 0.8.5b)
breadboards: 1

parts:
  Bauteil1 = Arduino Uno (Rev3)
  R1 = Rotary Potentiometer (Small)

nets:
  N1: Bauteil1.A0, R1.wiper
  N2: Bauteil1.GND, R1.leg1
  N3: Bauteil1.5V, R1.leg2

notes:
  /**
  * A very simple sketch by Fabian Morón Zirfas
  *
  *
  */
  int poti = A0; // the poti pin
  void setup(){
  Serial.begin(9600); // init Serial
  }
  void loop(){
  int potival = analogRead(poti); // read the poti
  Serial.println(potival); // print it
  delay(100);// wait a bit
  }
