# Fritzing sketch pulse_width_modulation (saved by Fritzing 0.8.3b)
breadboards: 1

parts:
  Bauteil1 = Arduino Uno (Rev3)
  R1 = Rotary Potentiometer (Small)
  LED1 = LED - 5mm [color="Red (633nm)" package="5 mm [THT]"]
  R2 = Resistor [tolerance=±5% resistance=220 package=THT]

nets:
  N1: Bauteil1.A0, R1.wiper
  N2: Bauteil1.GND, R1.leg2, LED1.cathode
  N3: Bauteil1.D9_PWM, R2.Pin_1
  N4: Bauteil1.5V, R1.leg1
  N5: LED1.anode, R2.Pin_0

notes:
  based on analogWrite example
  // http://arduino.cc/en/Reference/AnalogWrite
  int ledPin = 9; // LED connected to digital pin 9
  int analogPin = A0; // potentiometer connected to analog pin 3
  int val = 0; // variable to store the read value
  void setup(){
  pinMode(ledPin, OUTPUT); // sets the pin as output
  }
  void loop(){
  val = analogRead(analogPin); // read the input pin
  /**
  * analogRead values go from 0 to 1023
  * analogWrite values from 0 to 255
  */
  analogWrite(ledPin, val / 4);
  }
