# Fritzing sketch servomotor (saved by Fritzing 0.9.0b)
breadboards: 1

parts:
  J2 = Basic Servo
  Arduino3 = Arduino Uno (Rev3)

nets:
  GND: J2.gnd, Arduino3.GND
  VCC: J2.vcc, Arduino3.5V
  N1: J2.pulse, Arduino3.D9_PWM
