# Fritzing sketch servomotor (saved by Fritzing 0.8.5b)
breadboards: 2

parts:
  Arduino3 = Arduino Uno (Rev3)
  J2 = Basic Servo

nets:
  GND: Arduino3.GND, J2.gnd
  N1: Arduino3.D9_PWM, J2.pulse
  5V: Arduino3.5V, J2.vcc
