# Fritzing sketch stepper-h-bridge-l293d (saved by Fritzing 0.9.3b)
breadboards: 1

parts:
  Part1 = Arduino Uno (Rev3)
  IC1 = L293D [package=THT]
  M1 = Stepper Motor - Bipolar
  Power_plug1 = Power plug

nets:
  N1: Part1.D9_PWM, IC1.In_2
  N2: Part1.D10_PWM/SS, IC1.In_1
  N3: Part1.D11_PWM/MOSI, IC1.In_3
  N4: Part1.D12/MISO, IC1.In_4
  GND: Part1.GND, IC1.0V, Power_plug1.GND
  N5: Part1.5V, IC1.Enable_1, IC1.Enable_2
  VIN: Part1.VIN, IC1.+Vmotor, IC1.+V, Power_plug1.VCC
  N6: IC1.Out_1_(_Controlled_by_Enable_1_), M1.D
  N7: IC1.Out_2_(_Controlled_by_Enable_1_), M1.B
  N8: IC1.Out_3_(_Controlled_by_Enable_2_), M1.C
  N9: IC1.Out_4_(_Controlled_by_Enable_2_), M1.A
