# Fritzing sketch schmalzhaus-simple (saved by Fritzing 0.9.3b)
breadboards: 2

parts:
  Part1 = EasyDriver_v44
  Part2 = Arduino Uno (Rev3) - ICSP
  M1 = Stepper Motor - Bipolar
  Power_plug1 = Power plug
  Part3 = Arduino Uno (Rev3) - ICSP
  Part4 = EasyDriver_v44
  M2 = Stepper Motor - Bipolar
  Power_plug2 = Power plug

nets:
  GND: Part1.GND, Part2.GND, Power_plug1.GND
  N1: Part1.V+, Power_plug1.VCC
  N2: Part1.STEP, Part2.D9_PWM
  N3: Part1.DIR, Part2.D8
  N4: Part1.OUT2A, M1.A
  N5: Part1.OUT2B, M1.C
  N6: Part1.OUT1A, M1.B
  N7: Part1.OUT1B, M1.D
  GND_2: Part3.GND, Part4.GND, Power_plug2.GND
  N8: Part3.D8, Part4.DIR
  N9: Part3.D9_PWM, Part4.STEP
  VIN: Part3.VIN, Part4.V+, Power_plug2.VCC
  N10: Part4.OUT2A, M2.A
  N11: Part4.OUT2B, M2.C
  N12: Part4.OUT1A, M2.B
  N13: Part4.OUT1B, M2.D

notes:
  Normally a 12V DC power supply
  If you have a stepper with very high loads (> 250mA) you should not power your Arduino from the USB port. Use the power from the external power supply.(Like hown over there--->)
  This here only applies if your stepper draws more then 250mA
