# Fritzing sketch temperature (saved by Fritzing 0.8.3b)
breadboards: 1

parts:
  Bauteil1 = Arduino Uno (Rev3)
  T1 = TMP36 Temperature Sensor [package="TO92 [THT]"]

nets:
  N1: Bauteil1.A0, T1.Vout
  GND: Bauteil1.GND, T1.GND
  N2: Bauteil1.5V, T1.+Vs
